// Logisim project D_eksperyment.circ as structural Verilog: 1 circuit, main circuit main
module main (
  input  in_1
);

  wire clock_1_out, d_ff_1_q, d_ff_2_q, d_ff_3_q, xor_1_out, xor_2_out, xor_3_out;

  Clock clock_1 (.out(clock_1_out));
  xor xor_1 (xor_1_out, in_1, d_ff_1_q);
  D_Flip_Flop d_ff_1 (.clk(clock_1_out), .D(xor_1_out), .Q(d_ff_1_q));  // open: Qn, preset, en, reset
  xor xor_2 (xor_2_out, d_ff_1_q, d_ff_2_q);
  D_Flip_Flop d_ff_2 (.clk(clock_1_out), .D(xor_2_out), .Q(d_ff_2_q));  // open: Qn, preset, en, reset
  xor xor_3 (xor_3_out, d_ff_2_q, d_ff_3_q);
  D_Flip_Flop d_ff_3 (.clk(clock_1_out), .D(xor_3_out), .Q(d_ff_3_q));  // open: Qn, preset, en, reset
endmodule
