// Logisim project licznik_synchroniczny_mod_8.circ as structural Verilog: 1 circuit, main circuit main
module main (
  input  in_1
);

  wire and_1_out, and_2_out, and_3_out, and_4_out, and_5_out, and_6_out, clock_1_out, t_ff_1_q, t_ff_2_q,
       t_ff_3_q, t_ff_4_q, t_ff_5_q, t_ff_6_q;

  Clock clock_1 (.out(clock_1_out));
  T_Flip_Flop t_ff_1 (.clk(clock_1_out), .T(in_1), .Q(t_ff_1_q), .reset(and_2_out));  // open: Qn, preset, en
  and and_1 (and_1_out, t_ff_1_q, in_1);
  T_Flip_Flop t_ff_2 (.clk(clock_1_out), .T(and_1_out), .Q(t_ff_2_q), .reset(and_2_out));  // open: Qn, preset, en
  and and_2 (and_2_out, t_ff_3_q, in_1, t_ff_1_q);
  and and_3 (and_3_out, t_ff_1_q, t_ff_2_q, in_1);
  T_Flip_Flop t_ff_3 (.clk(clock_1_out), .T(and_3_out), .Q(t_ff_3_q), .reset(and_2_out));  // open: Qn, preset, en
  T_Flip_Flop t_ff_4 (.clk(clock_1_out), .T(t_ff_3_q), .Q(t_ff_4_q), .reset(and_6_out));  // open: Qn, preset, en
  and and_4 (and_4_out, t_ff_4_q, t_ff_2_q, t_ff_1_q, in_1);
  T_Flip_Flop t_ff_5 (.clk(clock_1_out), .T(and_4_out), .Q(t_ff_5_q), .reset(and_6_out));  // open: Qn, preset, en
  and and_5 (and_5_out, t_ff_4_q, t_ff_5_q, in_1);
  and and_6 (and_6_out, t_ff_6_q, t_ff_3_q, t_ff_4_q);
  T_Flip_Flop t_ff_6 (.clk(clock_1_out), .T(and_5_out), .Q(t_ff_6_q), .reset(and_6_out));  // open: Qn, preset, en

  // Notes on the sheet:
  //   Wszystkie poprzednie musza byc przepelnione (jeden) wiec jak sprawdzic to przy laczeniu szeregowym licznikow?
endmodule
