// Logisim project licznik_synchroniczny_na_D.circ as structural Verilog: 1 circuit, main circuit main
module main (
  input  in_1
);

  wire and_1_out, and_2_out, and_3_out, and_4_out, clock_1_out, d_ff_1_q, d_ff_2_q, d_ff_3_q, d_ff_4_q,
       xor_1_out, xor_2_out, xor_3_out, xor_4_out;

  Clock clock_1 (.out(clock_1_out));
  xor xor_1 (xor_1_out, in_1, d_ff_1_q);
  and and_1 (and_1_out, in_1, d_ff_1_q);
  D_Flip_Flop d_ff_1 (.clk(clock_1_out), .D(xor_1_out), .Q(d_ff_1_q), .reset(and_4_out));  // open: Qn, preset, en
  xor xor_2 (xor_2_out, and_1_out, d_ff_2_q);
  and and_2 (and_2_out, and_1_out, d_ff_2_q);
  D_Flip_Flop d_ff_2 (.clk(clock_1_out), .D(xor_2_out), .Q(d_ff_2_q), .reset(and_4_out));  // open: Qn, preset, en
  xor xor_3 (xor_3_out, and_2_out, d_ff_3_q);
  and and_3 (and_3_out, and_2_out, d_ff_3_q);
  and and_4 (and_4_out, d_ff_1_q, d_ff_2_q, d_ff_3_q);
  D_Flip_Flop d_ff_3 (.clk(clock_1_out), .D(xor_3_out), .Q(d_ff_3_q), .reset(and_4_out));  // open: Qn, preset, en
  xor xor_4 (xor_4_out, and_3_out, d_ff_4_q);
  D_Flip_Flop d_ff_4 (.clk(clock_1_out), .D(xor_4_out), .Q(d_ff_4_q), .reset(and_4_out));  // open: Qn, preset, en

  // Notes on the sheet:
  //   Licznik mod 8 bo zeruje na n-1
endmodule
