// Logisim project licznik_synchroniczny_zadanie_1_U1.circ as structural Verilog: 1 circuit, main circuit main
module main (
  input  Zgoda,
  input  RES,
  input  Zgoda_2,
  input  RES_2
);

  wire and_1_out, and_2_out, and_3_out, and_4_out, and_5_out, and_6_out, and_7_out, and_8_out, clock_1_out,
       clock_2_out, or_1_out, or_2_out, t_ff_1_q, t_ff_2_q, t_ff_2_qn, t_ff_3_q, t_ff_4_qn, t_ff_5_q,
       t_ff_6_qn, t_ff_7_q, t_ff_8_q;

  Clock clock_1 (.out(clock_1_out));
  Clock clock_2 (.out(clock_2_out));
  buf or_1 (or_1_out, RES_2);  // OR_Gate
  T_Flip_Flop t_ff_1 (.clk(clock_2_out), .T(Zgoda), .Q(t_ff_1_q), .reset(or_2_out));  // open: Qn, preset, en
  or or_2 (or_2_out, RES, and_7_out);
  T_Flip_Flop t_ff_2 (
    .clk(clock_1_out), .T(Zgoda_2), .Q(t_ff_2_q), .Qn(t_ff_2_qn), .reset(or_1_out));  // open: preset, en
  and and_1 (and_1_out, t_ff_1_q, Zgoda);
  and and_2 (and_2_out, t_ff_2_qn, Zgoda_2);
  T_Flip_Flop t_ff_3 (.clk(clock_2_out), .T(and_1_out), .Q(t_ff_3_q), .reset(or_2_out));  // open: Qn, preset, en
  T_Flip_Flop t_ff_4 (.clk(clock_1_out), .T(and_2_out), .Qn(t_ff_4_qn), .reset(or_1_out));  // open: Q, preset, en
  and and_3 (and_3_out, and_1_out, t_ff_3_q, Zgoda);
  and and_4 (and_4_out, and_2_out, t_ff_4_qn, Zgoda_2);
  T_Flip_Flop t_ff_5 (.clk(clock_2_out), .T(and_3_out), .Q(t_ff_5_q), .reset(or_2_out));  // open: Qn, preset, en
  T_Flip_Flop t_ff_6 (.clk(clock_1_out), .T(and_4_out), .Qn(t_ff_6_qn), .reset(or_1_out));  // open: Q, preset, en
  and and_5 (and_5_out, and_3_out, t_ff_5_q, Zgoda);
  T_Flip_Flop t_ff_7 (.clk(clock_1_out), .T(and_6_out), .Q(t_ff_7_q), .reset(or_1_out));  // open: Qn, preset, en
  and and_6 (and_6_out, and_4_out, t_ff_6_qn, Zgoda_2);
  T_Flip_Flop t_ff_8 (.clk(clock_2_out), .T(and_5_out), .Q(t_ff_8_q), .reset(or_2_out));  // open: Qn, preset, en
  and and_7 (and_7_out, Zgoda, t_ff_1_q, t_ff_8_q);
  and and_8 (and_8_out, t_ff_6_qn, t_ff_4_qn, Zgoda_2, t_ff_2_q, t_ff_7_q);

  // Notes on the sheet:
  //   Licznik w dol pelny zakres
  //   Licznik w gore mod 10
endmodule
