// Logisim project liczniki_synchroniczne.circ as structural Verilog: 1 circuit, main circuit main
module main (
  input  in_1,
  input  in_2,
  input  in_3
);

  wire and_1_out, and_2_out, and_3_out, and_4_out, and_5_out, and_7_out, and_8_out, and_9_out, and_10_out,
       and_11_out, clock_1_out, clock_2_out, clock_3_out, d_ff_1_q, d_ff_2_q, d_ff_3_q, j_k_ff_1_q, t_ff_1_q,
       t_ff_2_q, t_ff_3_q, t_ff_4_q, t_ff_5_q, t_ff_6_q, t_ff_7_q, t_ff_8_q, xor_1_out, xor_2_out, xor_3_out;

  Clock clock_1 (.out(clock_1_out));
  Clock clock_2 (.out(clock_2_out));
  xor xor_1 (xor_1_out, in_2, d_ff_1_q);
  T_Flip_Flop t_ff_1 (.clk(clock_1_out), .T(in_1), .Q(t_ff_1_q), .reset(and_5_out));  // open: Qn, preset, en
  D_Flip_Flop d_ff_1 (.clk(clock_2_out), .D(xor_1_out), .Q(d_ff_1_q));  // open: Qn, preset, en, reset
  and and_1 (and_1_out, t_ff_1_q, in_1);
  xor xor_2 (xor_2_out, d_ff_1_q, d_ff_2_q);
  T_Flip_Flop t_ff_2 (.clk(clock_1_out), .T(and_1_out), .Q(t_ff_2_q), .reset(and_5_out));  // open: Qn, preset, en
  D_Flip_Flop d_ff_2 (.clk(clock_2_out), .D(xor_2_out), .Q(d_ff_2_q));  // open: Qn, preset, en, reset
  and and_2 (and_2_out, and_1_out, t_ff_2_q, in_1);
  T_Flip_Flop t_ff_3 (.clk(clock_1_out), .T(and_2_out), .Q(t_ff_3_q), .reset(and_5_out));  // open: Qn, preset, en
  and and_3 (and_3_out, in_2, d_ff_2_q, d_ff_1_q, xor_3_out);
  xor xor_3 (xor_3_out, d_ff_2_q, d_ff_3_q);
  and and_4 (and_4_out, and_2_out, t_ff_3_q, in_1);
  D_Flip_Flop d_ff_3 (.clk(clock_2_out), .D(and_3_out), .Q(d_ff_3_q));  // open: Qn, preset, en, reset
  T_Flip_Flop t_ff_4 (.clk(clock_1_out), .T(and_4_out), .Q(t_ff_4_q), .reset(and_5_out));  // open: Qn, preset, en
  Clock clock_3 (.out(clock_3_out));
  and and_5 (and_5_out, t_ff_1_q, in_1, t_ff_4_q);
  // AND_Gate and_6 has open pins: in1=t_ff_4_q, in3=and_4_out, in4=in_1, out=open
  J_K_Flip_Flop j_k_ff_1 (.J(in_3), .clk(clock_3_out), .K(in_3), .Q(j_k_ff_1_q));  // open: Qn, preset, en, reset
  T_Flip_Flop t_ff_5 (.clk(clock_1_out), .T(and_5_out), .Q(t_ff_5_q), .reset(and_11_out));  // open: Qn, preset, en
  and and_7 (and_7_out, j_k_ff_1_q, in_3);
  and and_8 (and_8_out, t_ff_5_q, and_5_out);
  J_K_Flip_Flop j_k_ff_2 (.J(and_7_out), .clk(clock_3_out), .K(and_7_out));  // open: Q, Qn, preset, en, reset
  T_Flip_Flop t_ff_6 (.clk(clock_1_out), .T(and_8_out), .Q(t_ff_6_q), .reset(and_11_out));  // open: Qn, preset, en
  and and_9 (and_9_out, and_8_out, t_ff_6_q, and_5_out);
  T_Flip_Flop t_ff_7 (.clk(clock_1_out), .T(and_9_out), .Q(t_ff_7_q), .reset(and_11_out));  // open: Qn, preset, en
  and and_10 (and_10_out, and_9_out, t_ff_7_q, and_5_out);
  T_Flip_Flop t_ff_8 (.clk(clock_1_out), .T(and_10_out), .Q(t_ff_8_q), .reset(and_11_out));  // open: Qn, preset, en
  and and_11 (and_11_out, t_ff_5_q, and_5_out, t_ff_8_q);
  // AND_Gate and_12 has open pins: in1=t_ff_8_q, in3=and_10_out, in4=and_5_out, out=open

  // Notes on the sheet:
  //   Zgoda
  //   Pytania: 
  //   1
  //   2. Jak szeregowo polaczyc liczniki
  //   HOW
  //   Dla przerzutnikow D zgoda to poprzednie Q i biore Q z nastepnego
  //   2
  //   1. Jak skracam dla N to mam mod N zamiast mod N+1 jak wedlug wykladu
  //   Wykrywam stan 10 i mam MOD10 wedlug cwiczen powinenem wykrywac 9
  //   Gdy zliczam w dol to sprawdzam przepelnienie Q^ zamiast Q
  //   4
  //   8
  //   Zgoda
  //   Dla JK wystarczy polaczyc J i K po czym traktuje jak T
  //   1
  //   2
  //   4
  //   8
endmodule
