// Logisim project mod25.circ as structural Verilog: 1 circuit, main circuit main
module main (
  input  in_1
);

  wire and_1_out, and_2_out, clock_1_out, clock_2_out, nand_1_out, nand_2_out, nand_3_out, nand_4_out,
       not_1_out, not_2_out, not_3_out, not_4_out, not_5_out, not_6_out, or_1_out, or_2_out, t_ff_1_q,
       t_ff_1_qn, t_ff_2_q, t_ff_2_qn, t_ff_3_q, t_ff_3_qn, t_ff_4_q, t_ff_4_qn, t_ff_5_q, t_ff_5_qn,
       t_ff_6_q, t_ff_6_qn, t_ff_7_q, t_ff_7_qn, t_ff_8_q, t_ff_8_qn, t_ff_9_q, t_ff_10_q;

  Clock clock_1 (.out(clock_1_out));
  Clock clock_2 (.out(clock_2_out));
  T_Flip_Flop #(.trigger("falling")) t_ff_1 (
    .clk(clock_2_out), .T(in_1), .Q(t_ff_1_q), .Qn(t_ff_1_qn), .reset(or_1_out));  // open: preset, en
  T_Flip_Flop t_ff_2 (.clk(clock_1_out), .T(1'b1), .Q(t_ff_2_q), .Qn(t_ff_2_qn), .reset(or_2_out));  // open: preset, en
  T_Flip_Flop t_ff_3 (.clk(t_ff_2_qn), .T(1'b1), .Q(t_ff_3_q), .Qn(t_ff_3_qn), .reset(or_2_out));  // open: preset, en
  T_Flip_Flop #(.trigger("falling")) t_ff_4 (
    .clk(t_ff_1_qn), .T(in_1), .Q(t_ff_4_q), .Qn(t_ff_4_qn), .reset(or_1_out));  // open: preset, en
  T_Flip_Flop t_ff_5 (.clk(t_ff_3_qn), .T(1'b1), .Q(t_ff_5_q), .Qn(t_ff_5_qn), .reset(or_2_out));  // open: preset, en
  T_Flip_Flop #(.trigger("falling")) t_ff_6 (
    .clk(t_ff_4_qn), .T(in_1), .Q(t_ff_6_q), .Qn(t_ff_6_qn), .reset(or_1_out));  // open: preset, en
  or or_1 (or_1_out, nand_3_out, 1'b0);
  T_Flip_Flop t_ff_7 (.clk(t_ff_5_qn), .T(1'b1), .Q(t_ff_7_q), .Qn(t_ff_7_qn), .reset(or_2_out));  // open: preset, en
  or or_2 (or_2_out, nand_1_out, 1'b0);
  T_Flip_Flop #(.trigger("falling")) t_ff_8 (
    .clk(t_ff_6_qn), .T(in_1), .Q(t_ff_8_q), .Qn(t_ff_8_qn), .reset(or_1_out));  // open: preset, en
  not not_1 (not_1_out, t_ff_3_q);
  not not_2 (not_2_out, t_ff_5_q);
  not not_3 (not_3_out, t_ff_4_q);
  not not_4 (not_4_out, t_ff_6_q);
  T_Flip_Flop #(.trigger("falling")) t_ff_9 (
    .clk(t_ff_8_qn), .T(in_1), .Q(t_ff_9_q), .reset(or_1_out));  // open: Qn, preset, en
  T_Flip_Flop t_ff_10 (.clk(t_ff_7_qn), .T(1'b1), .Q(t_ff_10_q), .reset(or_2_out));  // open: Qn, preset, en
  and and_1 (and_1_out, t_ff_1_q, not_3_out, not_4_out, t_ff_8_q, t_ff_9_q);
  and and_2 (and_2_out, t_ff_2_q, not_1_out, not_2_out, t_ff_7_q, t_ff_10_q);
  nand nand_1 (nand_1_out, not_5_out, nand_2_out);
  nand nand_2 (nand_2_out, nand_1_out, clock_1_out);
  nand nand_3 (nand_3_out, not_6_out, nand_4_out);
  nand nand_4 (nand_4_out, nand_3_out, clock_2_out);
  not not_5 (not_5_out, and_2_out);
  not not_6 (not_6_out, and_1_out);

  // Notes on the sheet:
  //   Modulo 25 NKB, w górę, rising edge, skracanie
endmodule
