// Logisim project mod6_T.circ as structural Verilog: 1 circuit, main circuit main
module main (
  input  in_1,
  input  in_2
);

  wire and_1_out, clock_1_out, d_ff_1_q, d_ff_1_qn, d_ff_2_q, d_ff_2_qn, d_ff_3_q, nand_1_out, nand_2_out,
       nand_3_out, nand_4_out, nand_5_out;

  Clock clock_1 (.out(clock_1_out));
  nand nand_1 (nand_1_out, in_1, d_ff_1_q, d_ff_1_q);
  D_Flip_Flop d_ff_1 (
    .clk(clock_1_out), .D(nand_1_out), .Q(d_ff_1_q), .Qn(d_ff_1_qn), .reset(and_1_out));  // open: preset, en
  // OR_Gate or_1 has open pins: in1=nand_4_out, in4=in_2, out=open
  nand nand_2 (nand_2_out, d_ff_2_q, in_1);
  D_Flip_Flop d_ff_2 (
    .clk(d_ff_1_qn), .D(nand_2_out), .Q(d_ff_2_q), .Qn(d_ff_2_qn), .reset(and_1_out));  // open: preset, en
  nand nand_3 (nand_3_out, d_ff_3_q, in_1);
  D_Flip_Flop d_ff_3 (.clk(d_ff_2_qn), .D(nand_3_out), .Q(d_ff_3_q), .reset(and_1_out));  // open: Qn, preset, en
  nand nand_4 (nand_4_out, and_1_out, nand_5_out);
  nand nand_5 (nand_5_out, nand_4_out, clock_1_out);
  and and_1 (and_1_out, d_ff_2_q, d_ff_3_q);
endmodule
