// Logisim project modulo6_T.circ as structural Verilog: 1 circuit, main circuit main
module main (
  input  in_1,
  input  in_2
);

  wire and_1_out, and_2_out, t_ff_1_q, t_ff_2_q, t_ff_3_q;

  T_Flip_Flop t_ff_1 (.clk(in_2), .T(in_1), .Q(t_ff_1_q), .reset(and_2_out));  // open: Qn, preset, en
  LED led_1 (.in(t_ff_2_q));
  LED led_2 (.in(t_ff_3_q));
  T_Flip_Flop t_ff_2 (.clk(in_2), .T(t_ff_1_q), .Q(t_ff_2_q), .reset(and_2_out));  // open: Qn, preset, en
  LED led_3 (.in(t_ff_1_q));
  T_Flip_Flop t_ff_3 (.clk(in_2), .T(and_1_out), .Q(t_ff_3_q), .reset(and_2_out));  // open: Qn, preset, en
  and and_1 (and_1_out, t_ff_1_q, t_ff_2_q);
  and and_2 (and_2_out, t_ff_2_q, t_ff_3_q);
endmodule
